# Fritzing sketch sketch (saved by Fritzing 0.9.4)
breadboards: 1

parts:
  M5 = DC Motor  # not connected
  M6 = DC Motor  # not connected
  M7 = DC Motor  # not connected
  M8 = DC Motor  # not connected
  HC-SR04_Sensor_2 = HC-SR04 Ultrasonic Distance Sensor
  VCC6 = Battery block 9V  # not connected
  Part11 = Arduino Mega 2560 (Rev3)
  S1 = H-Bridge with L298N
  Part12 = FC-03 [chip_label=FC-03]
  S2 = H-Bridge with L298N
  Part13 = FC-03 [chip_label=FC-03]
  Part14 = FC-03 [chip_label=FC-03]
  Part15 = FC-03 [chip_label=FC-03]
  BAT3 = Battery Holders [package=battery-aa]
  BAT4 = Battery Holders [package=battery-aa]
  BAT5 = Battery Holders [package=battery-aa]
  BAT6 = Battery Holders [package=battery-aa]
  BAT7 = Battery Holders [package=battery-aa]
  BAT8 = Battery Holders [package=battery-aa]

nets:
  VCC: HC-SR04_Sensor_2.VCC, Part11.5V, Part12.pin_1, Part13.pin_1, Part14.pin_1, Part15.pin_1
  N1: HC-SR04_Sensor_2.TRIG, Part11.D5_PWM
  N2: HC-SR04_Sensor_2.ECHO, Part11.D6_PWM
  GND: HC-SR04_Sensor_2.GND, Part11.GND, S1.GND, Part12.pin_2, S2.GND, Part13.pin_2, Part14.pin_2, Part15.pin_2, BAT3.+, BAT4.+, BAT5.+, BAT6.+, BAT7.+, BAT8.+
  N3: Part11.D12_PWM, S2.ENA
  N4: Part11.D10_PWM, S1.ENA
  N5: Part11.D30, Part15.pin_3
  N6: Part11.D32, Part14.pin_3
  N7: Part11.D34, Part13.pin_3
  N8: Part11.D36, Part12.pin_3
  N9: Part11.D39, S2.IN1
  N10: Part11.D41, S2.IN2
  N11: Part11.D43, S2.IN3
  N12: Part11.D45, S2.IN4
  N13: Part11.D47, S1.IN1
  N14: Part11.D49, S1.IN2
  N15: Part11.D51, S1.IN3
  N16: Part11.D53, S1.IN4
  12V: S1.12V, S2.12V, BAT3.-, BAT4.-, BAT5.-, BAT6.-, BAT7.-, BAT8.-

custom parts:
  H-Bridge with L298N: h-bridge
  FC-03: FC-03, LM393 IR Speed Sensor Encoder
